# Fritzing sketch balloon (saved by Fritzing 0.9.4)
breadboards: 1

parts:
  Part1 = Arduino Mega 2560 (Rev3)
  SD_card_module1 = SD Card Module
  Part2 = InvenSense MPU6050
  DS1 = DS18B20 1-Wire Temperature Sensor [part_number=DS18B20]
  DHT1 = DHT22 Humidity and Temperature Sensor
  A1 = u-blox NEO-6M GPS Breakout
  Part3 = Adafruit BMP390 [part_number="Adafruit #4816"]

nets:
  N1: Part1.D21/SCL, Part2.SCL, Part3.SCK/SCL
  N2: Part1.D20/SDA, Part1.SDA, Part2.SDA, Part3.SDI/SDA
  N3: Part1.D19/RX1, A1.Pin_3
  N4: Part1.D18/TX1, A1.Pin_4
  N5: Part1.D10_PWM, SD_card_module1.CS
  N6: Part1.D9_PWM, DS1.DQ
  VCC: Part1.5V, SD_card_module1.+5, Part2.VCC, DS1.VDD, DHT1.VDD, A1.Pin_1, Part3.VCC
  GND: Part1.GND, SD_card_module1.GND, Part2.GND, DS1.GND, DHT1.GND, A1.Pin_2, Part3.GND
  N7: Part1.D2_PWM, DHT1.DATA
  N8: Part1.D50, SD_card_module1.MISO
  N9: Part1.D51, SD_card_module1.MOSI
  N10: Part1.D52, SD_card_module1.SCK

custom parts:
  SD Card Module: SD Card Module Slot Socket Reader For Arduino ARM MCU
  Adafruit BMP390: Bosch has been a leader in barometric pressure sensors, from the BMP085. BMP180, BMP280, BMP388... now we've got the next generation, the Adafruit BMP390 Precision Barometric Pressure and Altimeter Breakout. As you would expect, this sensor is similar to its earlier versions but even better. The BMP390 has better precision than ever, which makes it excellent for environmental sensing or as a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
